// Logisim project Ch7.circ as structural Verilog
module main (
);

  wire OpCode_p1, OpCode_p2, OpCode_p5, RegA_p7, RegB_p7, undriven_4, undriven_10, undriven_12;
  wire [1:0] undriven_6;
  wire [2:0] undriven_9, undriven_11;
  wire [15:0] Memory_data_out, n16_bit_alu_1_result, Registers_data_out, undriven, undriven_2, undriven_3,
       undriven_5, undriven_7, undriven_8;

  Control_Logic Control_Logic ();
  // _16_bit_register OpCode: pin names not known; wires that end beside it: OpCode_p1, OpCode_p2, OpCode_p2, OpCode_p1, OpCode_p5, OpCode_p5
  // _16_bit_register RegA: pin names not known; wires that end beside it: OpCode_p2, OpCode_p2, OpCode_p1, OpCode_p5, OpCode_p5, OpCode_p1, RegA_p7, RegA_p7
  // _16_bit_register RegB: pin names not known; wires that end beside it: OpCode_p5, OpCode_p5, OpCode_p1, RegA_p7, RegA_p7, OpCode_p1, RegB_p7, RegB_p7
  // _16_bit_register Param: pin names not known; wires that end beside it: RegB_p7, RegB_p7, OpCode_p1
  // _16_bit_register RegC: pin names not known; wires that end beside it: RegA_p7, RegA_p7, OpCode_p1, RegB_p7, RegB_p7, OpCode_p1
  Instruction_Register Instruction_Register (.In(undriven), .Out(undriven_5), .Clock(undriven_4));
  _16_BIT_ALU u_16_bit_alu_1 (
    .A(undriven_2), .B(undriven_3), .Result(n16_bit_alu_1_result), .Operation(undriven_6));  // open: Invert_A, Invert_B, CarryOut_Overflow
  _16_bit_8_word_register Registers (
    .Data_In(undriven_7), .Clock(undriven_10), .Data_Out(Registers_data_out), .Select_In(undriven_9));  // open: Select_Out
  _16_bit_8_word_register Memory (
    .Data_In(undriven_8), .Clock(undriven_12), .Data_Out(Memory_data_out), .Select_In(undriven_11));  // open: Select_Out
  Register_Note register_note_1 ();
endmodule

module _3_bit_register (
  input  Clock,
  input  [2:0] Input,
  input  Clock_2,
  output [2:0] Output
);

  D_Flip_Flop d_ff_1 (.clk(Clock), .D(Input[0]), .Q(Output[0]));  // open: Qn, preset, en, reset
  D_Flip_Flop d_ff_2 (.clk(Clock), .D(Input[1]), .Q(Output[1]));  // open: Qn, preset, en, reset
  D_Flip_Flop d_ff_3 (.clk(Clock), .D(Input[2]), .Q(Output[2]));  // open: Qn, preset, en, reset

  assign Clock_2 = Clock;
endmodule

// 16
module _16_bit_register (
  input  Clock,
  input  [15:0] Input,
  input  Clock_2,
  output [15:0] Output
);

  D_Flip_Flop d_ff_1 (.clk(Clock), .D(Input[14]), .Q(Output[14]));  // open: Qn, preset, en, reset
  D_Flip_Flop d_ff_2 (.clk(Clock), .D(Input[6]), .Q(Output[6]));  // open: Qn, preset, en, reset
  D_Flip_Flop d_ff_3 (.clk(Clock), .D(Input[8]), .Q(Output[8]));  // open: Qn, preset, en, reset
  D_Flip_Flop d_ff_4 (.clk(Clock), .D(Input[10]), .Q(Output[10]));  // open: Qn, preset, en, reset
  D_Flip_Flop d_ff_5 (.clk(Clock), .D(Input[12]), .Q(Output[12]));  // open: Qn, preset, en, reset
  D_Flip_Flop d_ff_6 (.clk(Clock), .D(Input[13]), .Q(Output[13]));  // open: Qn, preset, en, reset
  D_Flip_Flop d_ff_7 (.clk(Clock), .D(Input[15]), .Q(Output[15]));  // open: Qn, preset, en, reset
  D_Flip_Flop d_ff_8 (.clk(Clock), .D(Input[0]), .Q(Output[0]));  // open: Qn, preset, en, reset
  D_Flip_Flop d_ff_9 (.clk(Clock), .D(Input[2]), .Q(Output[2]));  // open: Qn, preset, en, reset
  D_Flip_Flop d_ff_10 (.clk(Clock), .D(Input[4]), .Q(Output[4]));  // open: Qn, preset, en, reset
  D_Flip_Flop d_ff_11 (.clk(Clock), .D(Input[5]), .Q(Output[5]));  // open: Qn, preset, en, reset
  D_Flip_Flop d_ff_12 (.clk(Clock), .D(Input[7]), .Q(Output[7]));  // open: Qn, preset, en, reset
  D_Flip_Flop d_ff_13 (.clk(Clock), .D(Input[9]), .Q(Output[9]));  // open: Qn, preset, en, reset
  D_Flip_Flop d_ff_14 (.clk(Clock), .D(Input[11]), .Q(Output[11]));  // open: Qn, preset, en, reset
  D_Flip_Flop d_ff_15 (.clk(Clock), .D(Input[1]), .Q(Output[1]));  // open: Qn, preset, en, reset
  D_Flip_Flop d_ff_16 (.clk(Clock), .D(Input[3]), .Q(Output[3]));  // open: Qn, preset, en, reset

  assign Clock_2 = Clock;
endmodule

module Instruction_Register (
  input  [15:0] In,
  input  [15:0] Out,
  input  Clock
);
endmodule
